# Fritzing sketch Schema (saved by Fritzing 0.9.3b)
breadboards: 1

parts:
  Composant2 = Arduino Nano (Rev3.0)
  OLED_I2C1 = OLED 128x64 I2C Monochrome Display
  KY-1 = Keyes Relay [package=THT]
  S1 = Square Pushbutton
  Power_plug1 = Power plug
  M1 = DC Motor
  S2 = Square Pushbutton
  LED1 = LED - 5mm [color="White (4500K)" package="5 mm [THT]"]
  LED2 = LED - 5mm [color="White (4500K)" package="5 mm [THT]"]
  LED3 = LED - 5mm [color="White (4500K)" package="5 mm [THT]"]
  LED4 = LED - 5mm [color="White (4500K)" package="5 mm [THT]"]
  R1 = Resistor [tolerance=±5% resistance=220 package=THT]
  R2 = Resistor [tolerance=±5% resistance=220 package=THT]
  R3 = Resistor [tolerance=±5% resistance=220 package=THT]
  R4 = Resistor [tolerance=±5% resistance=220 package=THT]
  R5 = Resistor [tolerance=±5% resistance=1k package="1206 [SMD]"]

nets:
  GND: Composant2.GND, OLED_I2C1.GND, KY-1.ground, S1.leg1, R1.Pin_0, R2.Pin_0, R3.Pin_0, R4.Pin_0
  N1: Composant2.D2, R5.Pin_0
  N2: Composant2.D3, KY-1.signal
  N3: Composant2.D4, S1.leg0
  N4: Composant2.D5, LED2.cathode, LED4.cathode
  N5: Composant2.D6, LED1.cathode, LED3.cathode
  5V: Composant2.5V, OLED_I2C1.VDD, KY-1.power, S2.leg1
  N6: Composant2.A5, OLED_I2C1.SCK
  N7: Composant2.A4, OLED_I2C1.SDA
  N8: KY-1.C, Power_plug1.VCC
  N9: KY-1.NO, M1.pin_2
  N10: Power_plug1.GND, M1.pin_1
  N11: S2.leg0, R5.Pin_1
  N12: LED1.anode, R1.Pin_1
  N13: LED2.anode, R2.Pin_1
  N14: LED3.anode, R3.Pin_1
  N15: LED4.anode, R4.Pin_1

notes:
  V = 12V max
  V = 5V Max
  4 LEDs Blanches + 4 Resistances 220 Ohms.
  Pompe a Liquide 12V /2A
  Groupement de LEDs:
  Groupe1: Leds 1 et 3.
  Groupe2: Leds 2 et 4.

custom parts:
  Keyes Relay: The Keyes 5V relay module is suitable for SCM development, home appliance control. It uses a 5V~12V TIL control signal which can control DC / AC signal.
