# Fritzing sketch Schema_Prototype (saved by Fritzing 1.0.4)
circuit board: 8.46667cm x 5.64444cm
breadboards: 1

parts:
  S1 = Square Pushbutton
  S2 = Square Pushbutton
  S3 = Square Pushbutton
  S4 = Square Pushbutton
  Composant1 = Arduino Mega 2560 (Rev3)
  JACK1 = 2.1mm Barrel Jack with Terminal Block
  KY-1 = Keyes Relay [package=THT]
  M1 = gear-motor [part_number="POMPE MEMBRANE - 12V/5A"]

nets:
  N1: S1.leg0, Composant1.D2_PWM
  N2: S1.leg1, S2.leg1, S3.leg1, S4.leg1, Composant1.GND, KY-1.ground
  N3: S2.leg0, Composant1.D3_PWM
  N4: S3.leg0, Composant1.D4_PWM
  N5: S4.leg0, Composant1.D5_PWM
  N6: Composant1.D9_PWM, KY-1.signal
  N7: Composant1.5V, KY-1.power
  N8: JACK1.POS, KY-1.C
  N9: JACK1.NEG, M1.pin_2
  N10: KY-1.NO, M1.pin_1

notes:
  !2 = BUTTON_HOLD_PIN
  !3= 1 seconde
  !4= BUTTON_BURST_PIN
  !5= BUTTON_RANDOM_PIN 30 secondes
  12 V - 5A

custom parts:
  Keyes Relay: The Keyes 5V relay module is suitable for SCM development, home appliance control. It uses a 5V~12V TIL control signal which can control DC / AC signal.
